// Logisim project atividade ula.circ as structural Verilog: 7 circuits, main circuit main
module main (
  input  [3:0] Y,
  input  [3:0] X,
  input  in_3,
  output out_4,
  output out_5,
  output [3:0] out_6,
  output out_7,
  output [3:0] out_8,
  output [7:0] out_9
);

  comparador comp (.x(X), .y(Y), .result(out_4));
  somador SOMA (.x(X), .y(Y), .carry_out(out_5), .result(out_6));
  subtrator SUB (.x(X), .controlador(in_3), .CarryOut(out_7), .out_5(out_8));  // open: y
  multi multi (.x(X), .y(Y), .result(out_9));
endmodule

// HA
module HalfAdder (
  input  X,
  input  Y,
  output S,
  output CarryOut
);

  xor xor_1 (S, X, Y);
  and and_1 (CarryOut, X, Y);
endmodule

// FA
module FullAdder (
  input  CarryIn,
  input  X,
  input  Y,
  output S,
  output CarryOut
);

  wire halfadder_1_carryout, halfadder_1_s, halfadder_2_carryout;

  HalfAdder halfadder_1 (.X(X), .Y(Y), .S(halfadder_1_s), .CarryOut(halfadder_1_carryout));
  HalfAdder halfadder_2 (.X(CarryIn), .Y(halfadder_1_s), .S(S), .CarryOut(halfadder_2_carryout));
  or or_1 (CarryOut, halfadder_2_carryout, halfadder_1_carryout);
endmodule

module comparador (
  input  [3:0] x,
  input  [3:0] y,
  output result
);

  wire and_1_out, and_2_out, xnor_1_out, xnor_2_out, xnor_3_out, xnor_4_out;

  xnor xnor_1 (xnor_1_out, x[0], y[0]);
  xnor xnor_2 (xnor_2_out, x[1], y[1]);
  xnor xnor_3 (xnor_3_out, x[2], y[2]);
  xnor xnor_4 (xnor_4_out, x[3], y[3]);
  and and_1 (and_1_out, xnor_1_out, xnor_2_out);
  and and_2 (and_2_out, xnor_3_out, xnor_4_out);
  and and_3 (result, and_1_out, and_2_out);
endmodule

module somador (
  input  [3:0] x,
  input  [3:0] y,
  output carry_out,
  output [3:0] result
);

  wire halfadder_1_carryout, halfadder_1_s, halfadder_2_s, halfadder_3_s, halfadder_4_carryout,
       halfadder_4_s, halfadder_5_carryout, halfadder_6_s, halfadder_8_carryout, halfadder_8_s,
       halfadder_9_carryout, halfadder_10_carryout;

  HalfAdder halfadder_1 (.X(x[2]), .Y(y[2]), .S(halfadder_1_s), .CarryOut(halfadder_1_carryout));
  HalfAdder halfadder_2 (.X(x[3]), .Y(y[3]), .S(halfadder_2_s));  // open: CarryOut
  HalfAdder halfadder_3 (.X(halfadder_1_carryout), .Y(halfadder_2_s), .S(halfadder_3_s));  // open: CarryOut
  HalfAdder halfadder_4 (
    .X(halfadder_8_carryout), .Y(halfadder_1_s), .S(halfadder_4_s), .CarryOut(halfadder_4_carryout));
  HalfAdder halfadder_5 (.X(halfadder_9_carryout), .Y(halfadder_4_s), .S(result[2]), .CarryOut(halfadder_5_carryout));
  HalfAdder halfadder_6 (.X(halfadder_4_carryout), .Y(halfadder_3_s), .S(halfadder_6_s));  // open: CarryOut
  HalfAdder halfadder_7 (.X(halfadder_5_carryout), .Y(halfadder_6_s), .S(result[3]), .CarryOut(carry_out));
  HalfAdder halfadder_8 (.X(x[1]), .Y(y[1]), .S(halfadder_8_s), .CarryOut(halfadder_8_carryout));
  HalfAdder halfadder_9 (.X(halfadder_10_carryout), .Y(halfadder_8_s), .S(result[1]), .CarryOut(halfadder_9_carryout));
  HalfAdder halfadder_10 (.X(x[0]), .Y(y[0]), .S(result[0]), .CarryOut(halfadder_10_carryout));
endmodule

module multi (
  input  [3:0] x,
  input  [3:0] y,
  output [7:0] result
);

  wire and_1_out, and_2_out, and_3_out, and_4_out, and_5_out, and_6_out, and_7_out, and_8_out, and_9_out,
       and_10_out, and_11_out, and_12_out, and_13_out, and_14_out, and_15_out, fulladder_1_carryout,
       fulladder_1_s, fulladder_3_carryout, fulladder_4_carryout, fulladder_4_s, fulladder_5_carryout,
       fulladder_5_s, fulladder_6_carryout, fulladder_6_s, fulladder_7_carryout, fulladder_8_carryout,
       fulladder_8_s, halfadder_1_carryout, halfadder_1_s, halfadder_2_carryout, halfadder_3_carryout,
       halfadder_4_carryout;

  HalfAdder halfadder_1 (.X(fulladder_4_carryout), .Y(and_3_out), .S(halfadder_1_s), .CarryOut(halfadder_1_carryout));
  and and_1 (and_1_out, x[3], y[2]);
  FullAdder fulladder_1 (
    .CarryIn(fulladder_5_carryout), .X(halfadder_1_carryout), .Y(and_1_out), .S(fulladder_1_s),
    .CarryOut(fulladder_1_carryout));
  and and_2 (and_2_out, x[3], y[3]);
  FullAdder fulladder_2 (
    .CarryIn(fulladder_3_carryout), .X(and_2_out), .Y(fulladder_1_carryout), .S(result[6]),
    .CarryOut(result[7]));
  and and_3 (and_3_out, x[3], y[1]);
  FullAdder fulladder_3 (
    .CarryIn(fulladder_7_carryout), .X(and_6_out), .Y(fulladder_1_s), .S(result[5]),
    .CarryOut(fulladder_3_carryout));
  and and_4 (and_4_out, x[3], y[0]);
  FullAdder fulladder_4 (
    .CarryIn(fulladder_8_carryout), .X(and_8_out), .Y(and_4_out), .S(fulladder_4_s),
    .CarryOut(fulladder_4_carryout));
  and and_5 (and_5_out, x[2], y[2]);
  FullAdder fulladder_5 (
    .CarryIn(fulladder_6_carryout), .X(halfadder_1_s), .Y(and_5_out), .S(fulladder_5_s),
    .CarryOut(fulladder_5_carryout));
  and and_6 (and_6_out, x[2], y[3]);
  and and_7 (and_7_out, x[2], y[0]);
  and and_8 (and_8_out, x[2], y[1]);
  and and_9 (and_9_out, x[1], y[2]);
  FullAdder fulladder_6 (
    .CarryIn(halfadder_3_carryout), .X(and_9_out), .Y(fulladder_4_s), .S(fulladder_6_s),
    .CarryOut(fulladder_6_carryout));
  HalfAdder halfadder_2 (.X(and_14_out), .Y(fulladder_6_s), .S(result[3]), .CarryOut(halfadder_2_carryout));
  FullAdder fulladder_7 (
    .CarryIn(halfadder_2_carryout), .X(and_11_out), .Y(fulladder_5_s), .S(result[4]),
    .CarryOut(fulladder_7_carryout));
  and and_10 (and_10_out, x[1], y[1]);
  FullAdder fulladder_8 (
    .CarryIn(halfadder_4_carryout), .X(and_10_out), .Y(and_7_out), .S(fulladder_8_s),
    .CarryOut(fulladder_8_carryout));
  and and_11 (and_11_out, x[1], y[3]);
  and and_12 (and_12_out, x[1], y[0]);
  and and_13 (and_13_out, x[0], y[2]);
  HalfAdder halfadder_3 (.X(and_13_out), .Y(fulladder_8_s), .S(result[2]), .CarryOut(halfadder_3_carryout));
  and and_14 (and_14_out, x[0], y[3]);
  and and_15 (and_15_out, x[0], y[1]);
  HalfAdder halfadder_4 (.X(and_15_out), .Y(and_12_out), .S(result[1]), .CarryOut(halfadder_4_carryout));
  and and_16 (result[0], x[0], y[0]);
endmodule

module subtrator (
  input  [3:0] x,
  input  [3:0] y,
  input  controlador,
  output CarryOut,
  output [3:0] out_5
);

  wire fulladder_2_carryout, fulladder_3_carryout, fulladder_4_carryout, xor_1_out, xor_2_out, xor_3_out,
       xor_4_out;

  FullAdder fulladder_1 (.CarryIn(fulladder_2_carryout), .X(x[3]), .Y(xor_1_out), .S(out_5[3]), .CarryOut(CarryOut));
  xor xor_1 (xor_1_out, controlador, y[3]);
  FullAdder fulladder_2 (
    .CarryIn(fulladder_3_carryout), .X(x[2]), .Y(xor_2_out), .S(out_5[2]), .CarryOut(fulladder_2_carryout));
  xor xor_2 (xor_2_out, controlador, y[2]);
  xor xor_3 (xor_3_out, controlador, y[1]);
  xor xor_4 (xor_4_out, controlador, y[0]);
  FullAdder fulladder_3 (
    .CarryIn(fulladder_4_carryout), .X(x[1]), .Y(xor_3_out), .S(out_5[1]), .CarryOut(fulladder_3_carryout));
  FullAdder fulladder_4 (.CarryIn(controlador), .X(x[0]), .Y(xor_4_out), .S(out_5[0]), .CarryOut(fulladder_4_carryout));
endmodule
