// Logisim project pd.circ as structural Verilog: 1 circuit, main circuit main
module main (
  output [3:0] imed,
  output [1:0] op_code,
  output [3:0] soma,
  output [3:0] sub,
  output [3:0] multi
);

  wire clock_1_out;
  wire [3:0] multiplexer_1_out, register_1_q, register_2_q;

  Register #(.width(4)) register_1 (.Q(register_1_q), .clk(clock_1_out));  // open: D, en, clr
  Clock clock_1 (.out(clock_1_out));
  RAM #(.addrWidth(4), .dataWidth(6)) ram_1 (.addr(register_1_q), .data({op_code, imed}));  // open: sel, clk, ld, clr
  Adder #(.width(4)) adder_1 (.a(register_2_q), .b(imed), .out(soma));  // open: cin, cout
  Subtractor #(.width(4)) subtractor_1 (.a(register_2_q), .b(imed), .out(sub));  // open: bin, bout
  Multiplier #(.width(4)) multiplier_1 (.a(register_2_q), .b(imed), .out(multi));  // open: cin, cout
  Multiplexer #(.select(2), .width(4)) multiplexer_1 (
    .in0(imed), .in1(soma), .in2(sub), .in3(multi), .out(multiplexer_1_out), .sel(op_code));  // open: en
  Register #(.width(4)) register_2 (.D(multiplexer_1_out), .Q(register_2_q), .clr(clock_1_out));  // open: en, clk
endmodule
